// Logisim project NANDToCPU.circ as structural Verilog
module Half_Adder (
  input  _00_01_10,
  input  in_2,
  output High,
  output Low
);

  and and_1 (High, _00_01_10, in_2);
  xor xor_1 (Low, _00_01_10, in_2);

  // Notes on the sheet:
  //   1 Bit Adder, No Carry
endmodule

module Full_Adder (
  input  Bit_0,
  input  Bit_1,
  input  Carry,
  output Sum,
  output C_out
);

  wire and_1_out, half_adder_1_high, half_adder_1_low;

  Half_Adder half_adder_1 (._00_01_10(Bit_1), .in_2(Carry), .High(half_adder_1_high), .Low(half_adder_1_low));
  and and_1 (and_1_out, Bit_0, half_adder_1_low);
  xor xor_1 (Sum, and_1_out, half_adder_1_high);
  xor xor_2 (C_out, Bit_0, half_adder_1_low);

  // Notes on the sheet:
  //   Full Adder
  //   00/01/10/11
endmodule

module _2_Bit_Adder (
  input  A1,
  input  A0,
  input  B1,
  input  B0,
  input  C_In,
  output S1,
  output S0,
  output C_Out
);

  wire full_adder_1_c_out, full_adder_1_sum, full_adder_2_sum, full_adder_3_sum;

  Full_Adder full_adder_1 (.Bit_0(A1), .Bit_1(B1), .Carry(1'b0), .Sum(full_adder_1_sum), .C_out(full_adder_1_c_out));
  Full_Adder full_adder_2 (.Bit_0(A0), .Bit_1(B0), .Carry(C_In), .Sum(full_adder_2_sum), .C_out(C_Out));
  Full_Adder full_adder_3 (
    .Bit_0(full_adder_1_c_out), .Bit_1(full_adder_2_sum), .Carry(1'b0), .Sum(full_adder_3_sum), .C_out(S0));
  or or_1 (S1, full_adder_1_sum, full_adder_3_sum);
endmodule

module _16_Bit_Adder (
  input  [7:0] A,
  input  [7:0] B,
  output [7:0] Sum,
  output Carry
);

  wire full_adder_1_c_out, full_adder_2_c_out, full_adder_3_c_out, full_adder_4_c_out, full_adder_5_c_out,
       full_adder_6_c_out, full_adder_7_c_out;

  Full_Adder full_adder_1 (.Bit_0(A[0]), .Bit_1(B[0]), .Carry(1'b0), .Sum(Sum[0]), .C_out(full_adder_1_c_out));
  Full_Adder full_adder_2 (
    .Bit_0(A[1]), .Bit_1(B[1]), .Carry(full_adder_1_c_out), .Sum(Sum[1]), .C_out(full_adder_2_c_out));
  Full_Adder full_adder_3 (
    .Bit_0(A[2]), .Bit_1(B[2]), .Carry(full_adder_2_c_out), .Sum(Sum[2]), .C_out(full_adder_3_c_out));
  Full_Adder full_adder_4 (
    .Bit_0(A[3]), .Bit_1(B[3]), .Carry(full_adder_3_c_out), .Sum(Sum[3]), .C_out(full_adder_4_c_out));
  Full_Adder full_adder_5 (
    .Bit_0(A[4]), .Bit_1(B[4]), .Carry(full_adder_4_c_out), .Sum(Sum[4]), .C_out(full_adder_5_c_out));
  Full_Adder full_adder_6 (
    .Bit_0(A[5]), .Bit_1(B[5]), .Carry(full_adder_5_c_out), .Sum(Sum[5]), .C_out(full_adder_6_c_out));
  Full_Adder full_adder_7 (
    .Bit_0(A[6]), .Bit_1(B[6]), .Carry(full_adder_6_c_out), .Sum(Sum[6]), .C_out(full_adder_7_c_out));
  Full_Adder full_adder_8 (.Bit_0(A[7]), .Bit_1(B[7]), .Carry(full_adder_7_c_out), .Sum(Sum[7]), .C_out(Carry));

  // Notes on the sheet:
  //   A Input
  //   B Input
  //   Output
  //   Least Significant Bit
endmodule
